// Logisim project ex4.circ as structural Verilog: 5 circuits, main circuit rot1
module RotRight (
  input  [15:0] INPUT0,
  input  [3:0] AMOUNT,
  output [15:0] OUTPUT0
);

  wire [15:0] rot1_2_out_2, rot1_3_out_2, rot1_4_out_2, rot1_5_out_2, rot1_6_out_2, rot1_7_out_2,
       rot1_8_out_2, rot2_1_out_2, rot2_3_out_2, rot2_4_out_2, rot2_5_out_2, rot2_7_out_2, rot2_8_out_2,
       rot4_1_out_2, rot4_5_out_2, rot4_6_out_2, rot4_8_out_2, rot8_1_out_2, t2, t4, t6, t8, t10, t12, t14,
       t16, t18, t20, t22, t24, t26, t28, t30, t32;

  rot8 rot8_1 (.in_1(INPUT0), .out_2(rot8_1_out_2));
  rot1 rot1_1 (.in_1(INPUT0), .out_2(t4));
  rot1 rot1_2 (.in_1(INPUT0), .out_2(rot1_2_out_2));
  rot4 rot4_1 (.in_1(INPUT0), .out_2(rot4_1_out_2));
  rot1 rot1_3 (.in_1(INPUT0), .out_2(rot1_3_out_2));
  rot2 rot2_1 (.in_1(INPUT0), .out_2(rot2_1_out_2));
  rot1 rot1_4 (.in_1(INPUT0), .out_2(rot1_4_out_2));
  rot8 rot8_2 (.in_1(rot8_1_out_2), .out_2(t2));
  rot2 rot2_2 (.in_1(INPUT0), .out_2(t6));
  rot1 rot1_5 (.in_1(INPUT0), .out_2(rot1_5_out_2));
  rot4 rot4_2 (.in_1(INPUT0), .out_2(t10));
  rot1 rot1_6 (.in_1(INPUT0), .out_2(rot1_6_out_2));
  rot2 rot2_3 (.in_1(INPUT0), .out_2(rot2_3_out_2));
  rot1 rot1_7 (.in_1(INPUT0), .out_2(rot1_7_out_2));
  rot1 rot1_8 (.in_1(INPUT0), .out_2(rot1_8_out_2));
  rot2 rot2_4 (.in_1(INPUT0), .out_2(rot2_4_out_2));
  rot2 rot2_5 (.in_1(rot1_4_out_2), .out_2(rot2_5_out_2));
  rot2 rot2_6 (.in_1(rot1_5_out_2), .out_2(t8));
  rot4 rot4_3 (.in_1(rot1_6_out_2), .out_2(t12));
  rot4 rot4_4 (.in_1(rot2_3_out_2), .out_2(t14));
  rot2 rot2_7 (.in_1(rot1_7_out_2), .out_2(rot2_7_out_2));
  rot8 rot8_3 (.in_1(INPUT0), .out_2(t18));
  rot2 rot2_8 (.in_1(rot1_2_out_2), .out_2(rot2_8_out_2));
  rot8 rot8_4 (.in_1(rot4_1_out_2), .out_2(t26));
  rot4 rot4_5 (.in_1(rot1_3_out_2), .out_2(rot4_5_out_2));
  rot4 rot4_6 (.in_1(rot2_1_out_2), .out_2(rot4_6_out_2));
  rot4 rot4_7 (.in_1(rot2_7_out_2), .out_2(t16));
  rot8 rot8_5 (.in_1(rot1_8_out_2), .out_2(t20));
  rot8 rot8_6 (.in_1(rot2_4_out_2), .out_2(t22));
  rot8 rot8_7 (.in_1(rot2_8_out_2), .out_2(t24));
  rot8 rot8_8 (.in_1(rot4_5_out_2), .out_2(t28));
  rot8 rot8_9 (.in_1(rot4_6_out_2), .out_2(t30));
  rot4 rot4_8 (.in_1(rot2_5_out_2), .out_2(rot4_8_out_2));
  rot8 rot8_10 (.in_1(rot4_8_out_2), .out_2(t32));
  Multiplexer #(.select(4), .width(16)) multiplexer_1 (
    .in0(t2), .in1(t4), .in2(t6), .in3(t8), .in4(t10), .in5(t12), .in6(t14), .in7(t16), .in8(t18), .in9(t20),
    .in10(t22), .in11(t24), .in12(t26), .in13(t28), .in14(t30), .in15(t32), .out(OUTPUT0), .sel(AMOUNT));

  // Other names for the same wires on the sheet: t1[15:0] = INPUT0; t3[15:0] = INPUT0; t5[15:0] = INPUT0;
  //   t7[15:0] = INPUT0; t9[15:0] = INPUT0; t11[15:0] = INPUT0; t13[15:0] = INPUT0; t15[15:0] = INPUT0;
  //   t17[15:0] = INPUT0; t19[15:0] = INPUT0; t21[15:0] = INPUT0; t23[15:0] = INPUT0; t25[15:0] = INPUT0;
  //   t27[15:0] = INPUT0; t29[15:0] = INPUT0; t31[15:0] = INPUT0; t33[3:0] = AMOUNT
endmodule

module rot1 (
  input  [15:0] in_1,
  output [15:0] out_2
);


  assign out_2 = {in_1[0], in_1[15:1]};

  // Other names for the same wires on the sheet: t1[14:0] = in_1[15:1]; t2 = in_1[0]
endmodule

module rot2 (
  input  [15:0] in_1,
  output [15:0] out_2
);


  assign out_2 = {in_1[1:0], in_1[15:2]};
endmodule

module rot4 (
  input  [15:0] in_1,
  output [15:0] out_2
);


  assign out_2 = {in_1[3:0], in_1[15:4]};
endmodule

module rot8 (
  input  [15:0] in_1,
  output [15:0] out_2
);


  assign out_2 = {in_1[7:0], in_1[15:8]};
endmodule
