// Logisim project ex2.circ as structural Verilog: 1 circuit, main circuit compute_BrUn
module compute_BrUn (
  input  [31:0] INSTRUCTION,
  output BrUn
);

  wire not_1_out, not_2_out, not_3_out;

  not not_1 (not_1_out, INSTRUCTION[2]);
  not not_2 (not_2_out, INSTRUCTION[3]);
  not not_3 (not_3_out, INSTRUCTION[4]);
  and and_1 (BrUn, not_1_out, not_2_out, not_3_out, INSTRUCTION[5], INSTRUCTION[6], INSTRUCTION[13]);
endmodule
