// Logisim project branch-comp.circ as structural Verilog: 1 circuit, main circuit branch_comp
module branch_comp (
  input  [31:0] BrData1,
  input  [31:0] BrData2,
  input  BrUn,
  output BrEq,
  output BrLt
);

  wire SIgnedBrEq, SignedBrLt, UnSIgnedBrEq, UnSIgnedBrLt;

  Comparator #(.width(32)) comparator_1 (.a(BrData1), .b(BrData2), .eq(SIgnedBrEq), .lt(SignedBrLt));  // open: gt
  Comparator #(.mode("unsigned"), .width(32)) comparator_2 (
    .a(BrData1), .b(BrData2), .eq(UnSIgnedBrEq), .lt(UnSIgnedBrLt));  // open: gt
  Multiplexer multiplexer_1 (.in0(SIgnedBrEq), .in1(UnSIgnedBrEq), .out(BrEq), .sel(BrUn));
  Multiplexer multiplexer_2 (.in0(SignedBrLt), .in1(UnSIgnedBrLt), .out(BrLt), .sel(BrUn));

  // Notes on the sheet:
  //   INPUTS to your circuit
  //   DON'T CHANGE THE LOCATIONS OF THE INPUTS AND OUTPUTS!
  //   OUTPUT from your circuit
endmodule
