// Logisim project control-logic.circ as structural Verilog: 1 circuit, main circuit control_logic
module control_logic (
  input  [31:0] Instruction,
  input  BrEq,
  input  BrLt,
  output PCSel,
  output RegWEn,
  output [2:0] ImmSel,
  output BrUn,
  output ASel,
  output BSel,
  output [3:0] ALUSel,
  output MemWEn,
  output [1:0] WBSel
);

  wire and_1_out, and_2_out, and_3_out, and_5_out, and_9_out, and_10_out, and_26_out, and_27_out, and_28_out,
       branch, Btype, Itype, Itype0, Itype1, Itype2, Itype4, Jtype, mul, mulh, mulsu, nor_1_out, nor_2_out,
       nor_3_out, nor_4_out, nor_5_out, nor_6_out, nor_7_out, nor_8_out, nor_9_out, nor_11_out, nor_12_out,
       nor_13_out, nor_14_out, nor_16_out, not_1_out, not_2_out, not_3_out, not_4_out, not_5_out, not_6_out,
       not_7_out, not_8_out, not_9_out, not_10_out, not_11_out, not_12_out, not_13_out, not_14_out,
       not_15_out, not_16_out, not_17_out, not_18_out, not_19_out, not_20_out, not_21_out, not_22_out,
       not_23_out, not_24_out, or_2_out, or_3_out, or_4_out, or_5_out, or_9_out, Rtype, sra0, Stype, sub0,
       Utype, Utype0, Utype1, WBSel1, WBSel2, WBSel3;
  wire [1:0] multiplexer_8_out, multiplexer_9_out;
  wire [2:0] multiplexer_10_out, multiplexer_11_out, multiplexer_13_out, multiplexer_14_out;
  wire [3:0] bit_extender_1_out, multiplexer_1_out, multiplexer_2_out, multiplexer_3_out, multiplexer_4_out,
       multiplexer_5_out, multiplexer_6_out;
  wire [15:0] rom_1_data;

  nor nor_1 (nor_1_out, Instruction[2], Instruction[3]);
  not not_1 (not_1_out, Instruction[4]);
  not not_2 (not_2_out, Instruction[3]);
  nor nor_2 (nor_2_out, Instruction[5], Instruction[6]);
  not not_3 (not_3_out, Instruction[4]);
  ROM #(.addrWidth(6), .dataWidth(16)) rom_1 (.data(rom_1_data));  // open: addr
  nor nor_3 (nor_3_out, Instruction[2], Instruction[3]);
  not not_4 (not_4_out, Instruction[6]);
  and and_1 (and_1_out, nor_1_out, not_1_out, Instruction[5], Instruction[6]);
  and and_2 (and_2_out, Instruction[2], not_2_out, Instruction[4], nor_2_out);
  and and_3 (and_3_out, Instruction[2], Instruction[3], not_3_out, Instruction[5], Instruction[6]);
  and and_4 (BSel, nor_3_out, Instruction[4], Instruction[5], not_4_out);
  or or_1 (ASel, and_1_out, and_2_out, and_3_out);
  or or_2 (or_2_out, Instruction[5], Instruction[6]);
  not not_5 (not_5_out, or_2_out);
  not not_6 (not_6_out, Instruction[13]);
  assign bit_extender_1_out = {{1{1'b0}}, Instruction[14:12]};  // Bit_Extender bit_extender_1
  or or_3 (or_3_out, Itype2, Btype, Jtype, Stype, Utype0);
  or or_4 (or_4_out, Instruction[4], not_5_out);
  and and_5 (and_5_out, Instruction[12], not_6_out, Instruction[14]);
  or or_5 (or_5_out, Rtype, Itype1);
  Multiplexer #(.width(4)) multiplexer_1 (
    .in0(bit_extender_1_out), .in1(4'b0000), .out(multiplexer_1_out), .sel(or_3_out));
  nor nor_4 (nor_4_out, Instruction[12], Instruction[13], Instruction[14]);
  not not_7 (not_7_out, Instruction[12]);
  or or_6 (RegWEn, Instruction[2], or_4_out);
  nor nor_5 (nor_5_out, Instruction[2], Instruction[3]);
  not not_8 (not_8_out, Instruction[6]);
  nor nor_6 (nor_6_out, Instruction[12], Instruction[13], Instruction[14]);
  and and_6 (sra0, and_5_out, Instruction[30], or_5_out);
  not not_9 (not_9_out, Instruction[14]);
  and and_7 (sub0, nor_6_out, Instruction[30], Rtype);
  Multiplexer #(.width(4)) multiplexer_2 (.in0(multiplexer_1_out), .in1(4'b1100), .out(multiplexer_2_out), .sel(sub0));
  Multiplexer #(.width(4)) multiplexer_3 (.in0(multiplexer_6_out), .in1(4'b1000), .out(multiplexer_3_out), .sel(mul));
  and and_8 (mul, nor_4_out, Instruction[25], Rtype);
  and and_9 (and_9_out, not_7_out, Instruction[13], Instruction[14]);
  and and_10 (and_10_out, Instruction[12], Instruction[13], not_9_out);
  and and_11 (Rtype, nor_5_out, Instruction[4], Instruction[5], not_8_out);
  Multiplexer #(.width(4)) multiplexer_4 (.in0(multiplexer_2_out), .in1(4'b1101), .out(multiplexer_4_out), .sel(sra0));
  Multiplexer #(.width(4)) multiplexer_5 (.in0(multiplexer_3_out), .in1(4'b1001), .out(multiplexer_5_out), .sel(mulh));
  and and_12 (mulh, and_9_out, Instruction[25], Rtype);
  and and_13 (mulsu, and_10_out, Instruction[25], Rtype);
  Multiplexer #(.width(4)) multiplexer_6 (
    .in0(multiplexer_4_out), .in1(4'b1111), .out(multiplexer_6_out), .sel(Utype1));
  Multiplexer #(.width(4)) multiplexer_7 (.in0(multiplexer_5_out), .in1(4'b1011), .out(ALUSel), .sel(mulsu));
  or or_7 (Utype, Utype0, Utype1);
  not not_10 (not_10_out, Instruction[2]);
  not not_11 (not_11_out, Instruction[3]);
  not not_12 (not_12_out, Instruction[4]);
  not not_13 (not_13_out, Instruction[3]);
  not not_14 (not_14_out, Instruction[3]);
  not not_15 (not_15_out, Instruction[6]);
  and and_14 (BrUn, not_10_out, not_11_out, not_12_out, Instruction[5], Instruction[6], Instruction[13]);
  nor nor_7 (nor_7_out, Instruction[5], Instruction[6]);
  nor nor_8 (nor_8_out, Instruction[2], Instruction[3]);
  nor nor_9 (nor_9_out, Instruction[4], Instruction[6]);
  nor nor_10 (Itype2, Instruction[2], Instruction[3], Instruction[4], Instruction[5], Instruction[6]);
  not not_16 (not_16_out, Instruction[4]);
  nor nor_11 (nor_11_out, Instruction[3], Instruction[4]);
  and and_15 (Utype0, Instruction[2], not_13_out, Instruction[4], nor_7_out);
  and and_16 (Utype1, Instruction[2], not_14_out, Instruction[5], not_15_out);
  nor nor_12 (nor_12_out, Instruction[2], Instruction[3], Instruction[5], Instruction[6]);
  nor nor_13 (nor_13_out, Instruction[2], Instruction[3], Instruction[5], Instruction[6]);
  or or_8 (Itype, Itype2, Itype1, Itype0, Itype4);
  nor nor_14 (nor_14_out, Instruction[2], Instruction[4], Instruction[3], Instruction[6]);
  and and_17 (Stype, nor_8_out, Instruction[5], nor_9_out);
  and and_18 (Itype1, nor_12_out, Instruction[4]);
  buf and_19 (Itype0, nor_13_out);  // AND_Gate
  and and_20 (Jtype, Instruction[2], Instruction[3], not_16_out, Instruction[5], Instruction[6]);
  and and_21 (Itype4, Instruction[2], nor_11_out, Instruction[5], Instruction[6]);
  and and_22 (MemWEn, nor_14_out, Instruction[5]);
  not not_17 (not_17_out, Instruction[3]);
  not not_18 (not_18_out, Instruction[6]);
  not not_19 (not_19_out, Instruction[4]);
  nor nor_15 (WBSel1, Instruction[2], Instruction[3], Instruction[4], Instruction[5], Instruction[6]);
  and and_23 (WBSel2, not_17_out, Instruction[4], not_18_out);
  and and_24 (WBSel3, Instruction[2], not_19_out, Instruction[5], Instruction[6]);
  Multiplexer #(.width(2)) multiplexer_8 (.in0(2'b01), .in1(2'b00), .out(multiplexer_8_out), .sel(WBSel1));
  not not_20 (not_20_out, Instruction[2]);
  not not_21 (not_21_out, Instruction[3]);
  not not_22 (not_22_out, Instruction[4]);
  nor nor_16 (nor_16_out, Instruction[12], Instruction[13], Instruction[14]);
  not not_23 (not_23_out, BrLt);
  Multiplexer #(.width(2)) multiplexer_9 (.in0(multiplexer_8_out), .in1(2'b10), .out(multiplexer_9_out), .sel(WBSel3));
  and and_25 (Btype, not_20_out, not_21_out, not_22_out, Instruction[5], Instruction[6]);
  not not_24 (not_24_out, Instruction[12]);
  Multiplexer #(.width(3)) multiplexer_10 (.in1(3'b000), .out(multiplexer_10_out), .sel(Itype));  // open: in0
  and and_26 (and_26_out, Btype, nor_16_out, BrEq);
  and and_27 (and_27_out, Btype, not_24_out, Instruction[14], BrLt);
  and and_28 (and_28_out, Btype, Instruction[12], Instruction[14], not_23_out);
  Multiplexer #(.width(3)) multiplexer_11 (
    .in0(multiplexer_10_out), .in1(3'b001), .out(multiplexer_11_out), .sel(Stype));
  Multiplexer #(.width(2)) multiplexer_12 (.in1(multiplexer_9_out), .out(WBSel), .sel(or_9_out));  // open: in0
  or or_9 (or_9_out, WBSel1, WBSel2, WBSel3);
  or or_10 (branch, and_26_out, and_27_out, and_28_out);
  Multiplexer #(.width(3)) multiplexer_13 (
    .in0(multiplexer_11_out), .in1(3'b010), .out(multiplexer_13_out), .sel(Btype));
  Multiplexer #(.width(3)) multiplexer_14 (
    .in0(multiplexer_13_out), .in1(3'b011), .out(multiplexer_14_out), .sel(Utype));
  Multiplexer #(.width(3)) multiplexer_15 (.in0(multiplexer_14_out), .in1(3'b100), .out(ImmSel), .sel(Jtype));
  or or_11 (PCSel, Jtype, branch, Itype4);

  // Other names for the same wires on the sheet: opcode[4:0] = Instruction[6:2]; func3[2:0] = Instruction[14:12];
  //   func7[6:0] = Instruction[31:25]

  // Notes on the sheet:
  //   INPUTS to your circuit
  //   Connect ROM Input here ->
  //   ROM FOR CONTROL LOGIC
  //   DON'T CHANGE THE LOCATIONS OF THE INPUTS AND OUTPUTS!
  //   This is only if you choose to do the ROM option
  //   CONNECT
  //   WIRE
  //   TO
  //   USE
  //   ROM
  //   OUTPUT from your circuit
  //   Reminder: If using ROM, use combinational logic for PCSel
endmodule
