// Logisim project cpu.circ as structural Verilog: 1 circuit, main circuit cpu
module cpu (
  input  clk,
  input  [31:0] Instruction,
  input  [31:0] MemReadData,
  output [31:0] MemAddress,
  output [31:0] ProgramCounter,
  output [31:0] ra,
  output [31:0] sp,
  output [31:0] t0,
  output [31:0] t1,
  output [31:0] t2,
  output [31:0] s0,
  output [31:0] s1,
  output [31:0] a0,
  output [3:0] MemWriteMask,
  output [31:0] MemWriteData
);

  wire ASel, BrEq, BrLt, BrUn, BSel, MemWEn, PCSel, PCSel2, RegWEn;
  wire [1:0] WBSel;
  wire [2:0] ImmSel;
  wire [3:0] ALUSel;
  wire [31:0] IMM, INSTpip_q, Instruction2, multiplexer_1_out, multiplexer_2_out, multiplexer_3_out, NextPC,
       NextPC2, PartialReadData, ProgramCounter2, ReadData1, ReadData2, WriteData;

  Multiplexer #(.width(32)) multiplexer_1 (.in0(NextPC), .in1(MemAddress), .out(multiplexer_1_out), .sel(PCSel));
  Register #(.width(32)) PC (.D(multiplexer_1_out), .clk(clk), .Q(ProgramCounter));  // open: en, clr
  Adder #(.width(32)) adder_1 (.a(ProgramCounter), .b(32'h4), .out(NextPC));  // open: cin, cout
  imm_gen imm_gen_1 (.Instruction(Instruction2), .ImmSel(ImmSel), .Immediate(IMM));
  control_logic control_logic_1 (
    .Instruction(Instruction2), .BrEq(BrEq), .BrLt(BrLt), .PCSel(PCSel), .RegWEn(RegWEn), .ImmSel(ImmSel),
    .BrUn(BrUn), .ASel(ASel), .BSel(BSel), .ALUSel(ALUSel), .MemWEn(MemWEn), .WBSel(WBSel));
  regfile regfile_1 (
    .ReadIndex1(Instruction2[19:15]), .ReadIndex2(Instruction2[24:20]), .WriteIndex(Instruction2[11:7]),
    .WriteData(WriteData), .RegWEn(RegWEn), .clk(clk), .ra(ra), .sp(sp), .t0(t0), .t1(t1), .t2(t2), .s0(s0),
    .s1(s1), .a0(a0), .ReadData1(ReadData1), .ReadData2(ReadData2));
  branch_comp branch_comp_1 (.BrData1(ReadData1), .BrData2(ReadData2), .BrUn(BrUn), .BrEq(BrEq), .BrLt(BrLt));
  Multiplexer #(.width(32)) multiplexer_2 (.in0(ReadData1), .in1(ProgramCounter2), .out(multiplexer_2_out), .sel(ASel));
  Multiplexer #(.width(32)) multiplexer_3 (.in0(IMM), .in1(ReadData2), .out(multiplexer_3_out), .sel(BSel));
  alu alu_1 (.A(multiplexer_2_out), .B(multiplexer_3_out), .ALUSel(ALUSel), .ALUResult(MemAddress));
  Register #(.width(32)) PCpip (.D(ProgramCounter), .clk(clk), .Q(ProgramCounter2));  // open: en, clr
  partial_store partial_store_1 (
    .Instruction(Instruction2), .MemAddress(MemAddress), .DataFromReg(ReadData2), .MemRW(MemWEn),
    .MemWriteMask(MemWriteMask), .DataToMem(MemWriteData));
  partial_load partial_load_1 (
    .Instruction(Instruction2), .MemAddress(MemAddress), .DataFromMem(MemReadData),
    .DataToReg(PartialReadData));
  Multiplexer #(.select(2), .width(32)) multiplexer_4 (
    .in0(PartialReadData), .in1(MemAddress), .in2(NextPC2), .out(WriteData), .sel(WBSel));  // open: in3
  Register #(.width(32)) INSTpip (.D(Instruction), .clk(clk), .Q(INSTpip_q));  // open: en, clr
  Register #(.width(1)) PCSelpip (.D(PCSel), .clk(clk), .Q(PCSel2));  // open: en, clr
  Multiplexer #(.width(32)) multiplexer_5 (.in0(INSTpip_q), .in1(32'h13), .out(Instruction2), .sel(PCSel2));
  Adder #(.width(32)) adder_2 (.a(ProgramCounter2), .b(32'h4), .out(NextPC2));  // open: cin, cout

  // Other names for the same wires on the sheet: ALUOut[31:0] = MemAddress; WriteIndex[4:0] = Instruction2[11:7];
  //   ReadIndex1[4:0] = Instruction2[19:15]; ReadIndex2[4:0] = Instruction2[24:20]

  // Notes on the sheet:
  //   To IMEM
  //   IMEM (do **NOT** move this)
  //   From IMEM
  //   Inputs/Outputs for testing. Do **NOT** move these.
  //   To DMEM
  //   DMEM (do **NOT** move this)
  //   From DMEM
endmodule
