// Logisim project imm-gen.circ as structural Verilog: 1 circuit, main circuit imm_gen
module imm_gen (
  input  [31:0] Instruction,
  input  [2:0] ImmSel,
  output [31:0] Immediate
);

  wire [11:0] demultiplexer_1_out3;
  wire [31:0] demultiplexer_1_out0, demultiplexer_1_out1, demultiplexer_1_out2, demultiplexer_1_out4, N1, N2,
       N3, N5;
  wire [31:12] N4;

  Demultiplexer #(.select(3), .width(32)) demultiplexer_1 (
    .out0(demultiplexer_1_out0), .out1(demultiplexer_1_out1), .out2(demultiplexer_1_out2),
    .out3({N4, demultiplexer_1_out3}), .out4(demultiplexer_1_out4), .in(Instruction), .sel(ImmSel));  // open: out5, out6, out7
  assign N1 = {{20{demultiplexer_1_out0[31]}}, demultiplexer_1_out0[31:20]};  // Bit_Extender bit_extender_1
  assign N2 = {{20{demultiplexer_1_out1[31]}}, {demultiplexer_1_out1[31:25], demultiplexer_1_out1[11:7]}};  // Bit_Extender bit_extender_2
  assign N3 = {{19{demultiplexer_1_out2[31]}}, {demultiplexer_1_out2[31], demultiplexer_1_out2[7], demultiplexer_1_out2[30:25], demultiplexer_1_out2[11:8], 1'b0}};  // Bit_Extender bit_extender_3
  assign N5 = {{11{demultiplexer_1_out4[31]}}, {demultiplexer_1_out4[31], demultiplexer_1_out4[19:12], demultiplexer_1_out4[20], demultiplexer_1_out4[30:21], 1'b0}};  // Bit_Extender bit_extender_4
  Multiplexer #(.select(3), .width(32)) multiplexer_1 (
    .in0(N1), .in1(N2), .in2(N3), .in3({N4, {12{1'b0}}}), .in4(N5), .out(Immediate), .sel(ImmSel));  // open: in5, in6, in7
  // AND_Gate and_1 is placed but not wired
  // AND_Gate and_2 is placed but not wired

  // Notes on the sheet:
  //   INPUTS to your circuit
  //   DON'T CHANGE THE LOCATIONS OF THE INPUTS AND OUTPUTS!
  //   OUTPUT from your circuit
endmodule
