// Logisim project partial-load.circ as structural Verilog: 1 circuit, main circuit partial_load
module partial_load (
  input  [31:0] Instruction,
  input  [31:0] MemAddress,
  input  [31:0] DataFromMem,
  output [31:0] DataToReg
);

  wire lb, lbu, lh, lhu, lw, nor_2_out, nor_3_out, nor_4_out, not_1_out, not_2_out, not_3_out, offset1,
       offset2, offset3;
  wire [7:0] demultiplexer_2_out0, demultiplexer_2_out1, multiplexer_5_out, multiplexer_7_out,
       multiplexer_8_out;
  wire [15:0] demultiplexer_1_out0, demultiplexer_1_out1, multiplexer_6_out;
  wire [31:0] multiplexer_1_out, multiplexer_2_out, multiplexer_3_out, signedByte, signedhalf, unsignedByte,
       unsignedhalf;

  nor nor_1 (lb, Instruction[12], Instruction[13], Instruction[14]);
  nor nor_2 (nor_2_out, Instruction[12], Instruction[13]);
  nor nor_3 (nor_3_out, Instruction[13], Instruction[14]);
  not not_1 (not_1_out, Instruction[13]);
  and and_1 (lbu, nor_2_out, Instruction[14]);
  and and_2 (lh, Instruction[12], nor_3_out);
  and and_3 (lhu, Instruction[12], not_1_out, Instruction[14]);
  and and_4 (lw, Instruction[13], nor_4_out);
  nor nor_4 (nor_4_out, Instruction[12], Instruction[14]);
  Multiplexer #(.width(32)) multiplexer_1 (.in0(DataFromMem), .in1(signedByte), .out(multiplexer_1_out), .sel(lb));
  not not_2 (not_2_out, MemAddress[1]);
  not not_3 (not_3_out, MemAddress[0]);
  Multiplexer #(.width(32)) multiplexer_2 (
    .in0(multiplexer_1_out), .in1(unsignedByte), .out(multiplexer_2_out), .sel(lbu));
  and and_5 (offset1, MemAddress[0], not_2_out);
  and and_6 (offset2, not_3_out, MemAddress[1]);
  and and_7 (offset3, MemAddress[0], MemAddress[1]);
  Multiplexer #(.width(32)) multiplexer_3 (
    .in0(multiplexer_2_out), .in1(signedhalf), .out(multiplexer_3_out), .sel(lh));
  Multiplexer #(.width(32)) multiplexer_4 (.in0(multiplexer_3_out), .in1(unsignedhalf), .out(DataToReg), .sel(lhu));
  Multiplexer #(.width(8)) multiplexer_5 (
    .in0(DataFromMem[7:0]), .in1(DataFromMem[15:8]), .out(multiplexer_5_out), .sel(offset1));
  Multiplexer #(.width(16)) multiplexer_6 (
    .in0(DataFromMem[15:0]), .in1(DataFromMem[31:16]), .out(multiplexer_6_out), .sel(offset2));
  Multiplexer #(.width(8)) multiplexer_7 (
    .in0(multiplexer_5_out), .in1(DataFromMem[23:16]), .out(multiplexer_7_out), .sel(offset2));
  Demultiplexer #(.width(16)) demultiplexer_1 (
    .out0(demultiplexer_1_out0), .out1(demultiplexer_1_out1), .in(multiplexer_6_out), .sel(lhu));
  Multiplexer #(.width(8)) multiplexer_8 (
    .in0(multiplexer_7_out), .in1(DataFromMem[31:24]), .out(multiplexer_8_out), .sel(offset3));
  assign signedhalf = {{16{demultiplexer_1_out0[15]}}, demultiplexer_1_out0};  // Bit_Extender bit_extender_1
  assign unsignedhalf = {{16{1'b0}}, demultiplexer_1_out1};  // Bit_Extender bit_extender_2
  Demultiplexer #(.width(8)) demultiplexer_2 (
    .out0(demultiplexer_2_out0), .out1(demultiplexer_2_out1), .in(multiplexer_8_out), .sel(lbu));
  assign signedByte = {{24{demultiplexer_2_out0[7]}}, demultiplexer_2_out0};  // Bit_Extender bit_extender_3
  assign unsignedByte = {{24{1'b0}}, demultiplexer_2_out1};  // Bit_Extender bit_extender_4

  // Other names for the same wires on the sheet: func7[4:0] = Instruction[6:2]; func3[2:0] = Instruction[14:12];
  //   offset[1:0] = MemAddress[1:0]

  // Notes on the sheet:
  //   INPUTS to your circuit
  //   DON'T CHANGE THE LOCATIONS OF THE INPUTS AND OUTPUTS!
  //   OUTPUT from your circuit
endmodule
