// Logisim project partial-store.circ as structural Verilog: 1 circuit, main circuit partial_store
module partial_store (
  input  [31:0] Instruction,
  input  [31:0] MemAddress,
  input  [31:0] DataFromReg,
  input  MemRW,
  output [3:0] MemWriteMask,
  output [31:0] DataToMem
);

  wire nor_2_out, not_1_out, not_2_out, offset1, offset2, offset3, sb, sh;
  wire [3:0] ByteWrite, HalfWrite, multiplexer_2_out, multiplexer_3_out, multiplexer_9_out;
  wire [7:0] undriven_3, undriven_4, undriven_5, undriven_6, undriven_7, undriven_8, undriven_9, undriven_10,
       undriven_11, undriven_12, undriven_13, undriven_14;
  wire [15:0] undriven, undriven_2;
  wire [31:0] ByteWriteData, HalfWriteData, multiplexer_4_out, multiplexer_6_out, multiplexer_8_out;

  nor nor_1 (sb, Instruction[12], Instruction[13], Instruction[14]);
  nor nor_2 (nor_2_out, Instruction[13], Instruction[14]);
  not not_1 (not_1_out, MemAddress[1]);
  and and_1 (sh, Instruction[12], nor_2_out);
  and and_2 (offset1, MemAddress[0], not_1_out);
  not not_2 (not_2_out, MemAddress[0]);
  and and_3 (offset2, not_2_out, MemAddress[1]);
  and and_4 (offset3, MemAddress[0], MemAddress[1]);
  Multiplexer #(.width(4)) multiplexer_1 (
    .in0({2'b00, {2{MemRW}}}), .in1({{2{MemRW}}, 2'b00}), .out(HalfWrite), .sel(offset2));
  Multiplexer #(.width(4)) multiplexer_2 (
    .in0({3'b000, MemRW}), .in1({2'b00, MemRW, 1'b0}), .out(multiplexer_2_out), .sel(offset1));
  Multiplexer #(.width(4)) multiplexer_3 (.in0({4{MemRW}}), .in1(HalfWrite), .out(multiplexer_3_out), .sel(sh));
  Multiplexer #(.width(32)) multiplexer_4 (.in0(DataFromReg), .in1(HalfWriteData), .out(multiplexer_4_out), .sel(sh));
  Multiplexer #(.width(32)) multiplexer_5 (
    .in0({undriven, DataFromReg[15:0]}), .in1({DataFromReg[15:0], undriven_2}), .out(HalfWriteData),
    .sel(offset2));
  Multiplexer #(.width(32)) multiplexer_6 (
    .in0({undriven_5, undriven_4, undriven_3, DataFromReg[7:0]}),
    .in1({undriven_8, undriven_7, DataFromReg[7:0], undriven_6}), .out(multiplexer_6_out), .sel(offset1));
  Multiplexer #(.width(4)) multiplexer_7 (.in0(multiplexer_3_out), .in1(ByteWrite), .out(MemWriteMask), .sel(sb));
  Multiplexer #(.width(32)) multiplexer_8 (
    .in0(multiplexer_6_out), .in1({undriven_11, DataFromReg[7:0], undriven_10, undriven_9}),
    .out(multiplexer_8_out), .sel(offset2));
  Multiplexer #(.width(4)) multiplexer_9 (
    .in0(multiplexer_2_out), .in1({1'b0, MemRW, 2'b00}), .out(multiplexer_9_out), .sel(offset2));
  Multiplexer #(.width(32)) multiplexer_10 (.in0(multiplexer_4_out), .in1(ByteWriteData), .out(DataToMem), .sel(sb));
  Multiplexer #(.width(32)) multiplexer_11 (
    .in0(multiplexer_8_out), .in1({DataFromReg[7:0], undriven_14, undriven_13, undriven_12}),
    .out(ByteWriteData), .sel(offset3));
  Multiplexer #(.width(4)) multiplexer_12 (
    .in0(multiplexer_9_out), .in1({MemRW, 3'b000}), .out(ByteWrite), .sel(offset3));

  // Other names for the same wires on the sheet: FullWrite[3:0] = {4{MemRW}}; func3[2:0] = Instruction[14:12];
  //   offset[1:0] = MemAddress[1:0]

  // Notes on the sheet:
  //   INPUTS to your circuit
  //   DON'T CHANGE THE LOCATIONS OF THE INPUTS AND OUTPUTS!
  //   OUTPUT from your circuit
endmodule
