// Logisim project regfile.circ as structural Verilog: 1 circuit, main circuit regfile
module regfile (
  input  [4:0] ReadIndex1,
  input  [4:0] ReadIndex2,
  input  [4:0] WriteIndex,
  input  [31:0] WriteData,
  input  RegWEn,
  input  clk,
  output [31:0] ra,
  output [31:0] sp,
  output [31:0] t0,
  output [31:0] t1,
  output [31:0] t2,
  output [31:0] s0,
  output [31:0] s1,
  output [31:0] a0,
  output [31:0] ReadData1,
  output [31:0] ReadData2
);

  wire W1, W2, W3, W4, W5, W6, W7, W8, W9, W10, W11, W12, W13, W14, W15, W16, W17, W18, W19, W20, W21, W22,
       W23, W24, W25, W26, W27, W28, W29, W30, W31;
  wire [31:0] O0, O3, O4, O11, O12, O13, O14, O15, O16, O17, O18, O19, O20, O21, O22, O23, O24, O25, O26,
       O27, O28, O29, O30, O31;

  Demultiplexer #(.select(5)) demultiplexer_1 (
    .out1(W1), .out2(W2), .out3(W3), .out4(W4), .out5(W5), .out6(W6), .out7(W7), .out8(W8), .out9(W9),
    .out10(W10), .out11(W11), .out12(W12), .out13(W13), .out14(W14), .out15(W15), .out16(W16), .out17(W17),
    .out18(W18), .out19(W19), .out20(W20), .out21(W21), .out22(W22), .out23(W23), .out24(W24), .out25(W25),
    .out26(W26), .out27(W27), .out28(W28), .out29(W29), .out30(W30), .out31(W31), .in(RegWEn),
    .sel(WriteIndex));  // open: out0
  Register #(.width(32)) register_1 (.D(WriteData), .en(W1), .clk(clk), .Q(ra));  // open: clr
  Register #(.width(32)) register_2 (.Q(O0));  // open: D, en, clk, clr
  Register #(.width(32)) register_3 (.D(WriteData), .en(W2), .clk(clk), .Q(sp));  // open: clr
  Register #(.width(32)) register_4 (.D(WriteData), .en(W5), .clk(clk), .Q(t0));  // open: clr
  Register #(.width(32)) register_5 (.D(WriteData), .en(W6), .clk(clk), .Q(t1));  // open: clr
  Register #(.width(32)) register_6 (.D(WriteData), .en(W7), .clk(clk), .Q(t2));  // open: clr
  Register #(.width(32)) register_7 (.D(WriteData), .en(W8), .clk(clk), .Q(s0));  // open: clr
  Register #(.width(32)) register_8 (.D(WriteData), .en(W9), .clk(clk), .Q(s1));  // open: clr
  Register #(.width(32)) register_9 (.D(WriteData), .en(W10), .clk(clk), .Q(a0));  // open: clr
  Register #(.width(32)) register_10 (.D(WriteData), .en(W11), .clk(clk), .Q(O11));  // open: clr
  Register #(.width(32)) register_11 (.D(WriteData), .en(W12), .clk(clk), .Q(O12));  // open: clr
  Register #(.width(32)) register_12 (.D(WriteData), .en(W13), .clk(clk), .Q(O13));  // open: clr
  Register #(.width(32)) register_13 (.D(WriteData), .en(W14), .clk(clk), .Q(O14));  // open: clr
  Register #(.width(32)) register_14 (.D(WriteData), .en(W3), .clk(clk), .Q(O3));  // open: clr
  Register #(.width(32)) register_15 (.D(WriteData), .en(W4), .clk(clk), .Q(O4));  // open: clr
  Register #(.width(32)) register_16 (.D(WriteData), .en(W24), .clk(clk), .Q(O24));  // open: clr
  Register #(.width(32)) register_17 (.D(WriteData), .en(W23), .clk(clk), .Q(O23));  // open: clr
  Register #(.width(32)) register_18 (.D(WriteData), .en(W22), .clk(clk), .Q(O22));  // open: clr
  Register #(.width(32)) register_19 (.D(WriteData), .en(W18), .clk(clk), .Q(O18));  // open: clr
  Register #(.width(32)) register_20 (.D(WriteData), .en(W17), .clk(clk), .Q(O17));  // open: clr
  Register #(.width(32)) register_21 (.D(WriteData), .en(W16), .clk(clk), .Q(O16));  // open: clr
  Register #(.width(32)) register_22 (.D(WriteData), .en(W15), .clk(clk), .Q(O15));  // open: clr
  Register #(.width(32)) register_23 (.D(WriteData), .en(W27), .clk(clk), .Q(O27));  // open: clr
  Register #(.width(32)) register_24 (.D(WriteData), .en(W26), .clk(clk), .Q(O26));  // open: clr
  Register #(.width(32)) register_25 (.D(WriteData), .en(W25), .clk(clk), .Q(O25));  // open: clr
  Register #(.width(32)) register_26 (.D(WriteData), .en(W21), .clk(clk), .Q(O21));  // open: clr
  Register #(.width(32)) register_27 (.D(WriteData), .en(W20), .clk(clk), .Q(O20));  // open: clr
  Register #(.width(32)) register_28 (.D(WriteData), .en(W19), .clk(clk), .Q(O19));  // open: clr
  Register #(.width(32)) register_29 (.D(WriteData), .en(W28), .clk(clk), .Q(O28));  // open: clr
  Register #(.width(32)) register_30 (.D(WriteData), .en(W29), .clk(clk), .Q(O29));  // open: clr
  Register #(.width(32)) register_31 (.D(WriteData), .en(W30), .clk(clk), .Q(O30));  // open: clr
  Register #(.width(32)) register_32 (.D(WriteData), .en(W31), .clk(clk), .Q(O31));  // open: clr
  Register #(.width(32)) register_33 (.D(WriteData), .clk(clk));  // open: en, Q, clr
  Multiplexer #(.select(5), .width(32)) multiplexer_1 (
    .in0(O0), .in1(ra), .in2(sp), .in3(O3), .in4(O4), .in5(t0), .in6(t1), .in7(t2), .in8(s0), .in9(s1),
    .in10(a0), .in11(O11), .in12(O12), .in13(O13), .in14(O14), .in15(O15), .in16(O16), .in17(O17),
    .in18(O18), .in19(O19), .in20(O20), .in21(O21), .in22(O22), .in23(O23), .in24(O24), .in25(O25),
    .in26(O26), .in27(O27), .in28(O28), .in29(O29), .in30(O30), .in31(O31), .out(ReadData1), .sel(ReadIndex1));
  Multiplexer #(.select(5), .width(32)) multiplexer_2 (
    .in0(O0), .in1(ra), .in2(sp), .in3(O3), .in4(O4), .in5(t0), .in6(t1), .in7(t2), .in8(s0), .in9(s1),
    .in10(a0), .in11(O11), .in12(O12), .in13(O13), .in14(O14), .in15(O15), .in16(O16), .in17(O17),
    .in18(O18), .in19(O19), .in20(O20), .in21(O21), .in22(O22), .in23(O23), .in24(O24), .in25(O25),
    .in26(O26), .in27(O29), .in28(O28), .in29(O29), .in30(O30), .in31(O31), .out(ReadData2), .sel(ReadIndex2));

  // Notes on the sheet:
  //   INPUTS to your circuit
  //   DON'T CHANGE THE LOCATIONS OF THE INPUTS AND OUTPUTS!
  //   These are DEBUG/TEST outputs from your circuit.
  //   OUTPUTS from your circuit
endmodule
